// Logisim project MIPS.circ as structural Verilog: 1 circuit, main circuit main
module main (
);

  wire ALUSrc, and_1_out, BNE, Branch, Clear, Clock, Exception, exception_t, ExcOut, Jump, JumpRegister,
       Link, MemRead, MemtoReg, MemWrite, multiplexer_4_out, not_1_out, RegDst, WriteReg, Zero;
  wire [3:0] Op;
  wire [4:0] multiplexer_7_out, multiplexer_8_out, rd, rs, rt, shamt, WR, WR_expect;
  wire [5:0] funct, opcode;
  wire [15:0] imm16;
  wire [25:0] addr;
  wire [31:0] adder_1_out, EPC, imm32, LD, LD1, LD2, mfc0R, multiplexer_1_out, multiplexer_2_out,
       multiplexer_3_out, multiplexer_5_out, multiplexer_6_out, multiplexer_9_out, multiplexer_12_out,
       multiplexer_13_out, PC_4, PC_q, result, undriven, WD;

  Multiplexer #(.width(32), .enable("false")) multiplexer_1 (
    .in0(multiplexer_2_out), .out(multiplexer_1_out), .sel(Jump));  // open: in1
  Multiplexer #(.width(32), .enable("false")) multiplexer_2 (
    .in0(multiplexer_6_out), .in1(LD1), .out(multiplexer_2_out), .sel(JumpRegister));
  not not_1 (not_1_out, Zero);
  Multiplexer #(.width(32), .enable("false")) multiplexer_3 (
    .in0(multiplexer_1_out), .in1(32'h80000180), .out(multiplexer_3_out), .sel(Exception));
  Multiplexer #(.enable("false")) multiplexer_4 (.in0(Zero), .in1(not_1_out), .out(multiplexer_4_out), .sel(BNE));
  Multiplexer #(.width(32), .enable("false")) multiplexer_5 (
    .in0(multiplexer_3_out), .in1(EPC), .out(multiplexer_5_out), .sel(ExcOut));
  Multiplexer #(.width(32), .enable("false")) multiplexer_6 (
    .in0(PC_4), .in1(adder_1_out), .out(multiplexer_6_out), .sel(and_1_out));
  and and_1 (and_1_out, multiplexer_4_out, Branch);
  Register #(.width(32)) PC (.D(multiplexer_5_out), .en(1'b1), .Q(PC_q), .clk(Clock), .clr(Clear));
  Adder #(.width(32)) adder_1 (.a({imm32[29:0], 2'b00}), .b(PC_4), .out(adder_1_out));  // open: cin, cout
  Adder #(.width(32)) adder_2 (.a(32'h4), .b(PC_q), .out(PC_4));  // open: cin, cout
  mem_instr mem_instr_1 (.INPUT(undriven), .OUTPUT(PC_q));
  \decodificador_de_instrução  \decodificador_de_instrução_1  (
    .\Instrução (undriven), .opcode(opcode), .RS(rs), .RT(rt), .RD(rd), .shamt(shamt), .funct(funct),
    .imm(imm16), .addr(addr));
  Multiplexer #(.width(5), .enable("false")) multiplexer_7 (.in0(rt), .in1(rd), .out(multiplexer_7_out), .sel(RegDst));
  Multiplexer #(.width(5), .enable("false")) multiplexer_8 (
    .in0(multiplexer_7_out), .in1(WR_expect), .out(multiplexer_8_out), .sel(ExcOut));
  Multiplexer #(.width(32), .enable("false")) multiplexer_9 (
    .in0(multiplexer_12_out), .in1(mfc0R), .out(multiplexer_9_out), .sel(ExcOut));
  extensor extensor_1 (.INPUT(imm16), .OUTPUT(imm32));
  Multiplexer #(.width(5), .enable("false")) multiplexer_10 (
    .in0(multiplexer_8_out), .in1({5{1'b1}}), .out(WR), .sel(Link));
  Multiplexer #(.width(32), .enable("false")) multiplexer_11 (
    .in0(multiplexer_9_out), .in1(PC_4), .out(WD), .sel(Link));
  banco_de_registradores banco_de_registradores_1 (
    .CLK(Clock), .EW(WriteReg), .WD(WD), .LR1(rs), .LR2(rt), .WR(WR), .LD1(LD1), .LD2(LD2));
  Multiplexer #(.width(32), .enable("false")) multiplexer_12 (
    .in0(result), .in1(LD), .out(multiplexer_12_out), .sel(MemtoReg));
  ULA ula_1 (
    .Result(result), .Overflow(exception_t), .Zero(Zero), .A(LD1), .B(multiplexer_13_out), .Shamt(shamt),
    .\Operação (Op));
  Multiplexer #(.width(32), .enable("false")) multiplexer_13 (
    .in0(LD2), .in1(imm32), .out(multiplexer_13_out), .sel(ALUSrc));
  mem_data mem_data_1 (.address(result), .\input (LD2), .str(MemRead), .ld(MemWrite), .clk(Clock), .\output (LD));
endmodule
